// Logisim project CPU.circ as structural Verilog: 3 circuits, main circuit main
module main (
  input  Clear
);

  wire controlunit_1_clr, controlunit_1_dalu, controlunit_1_dbuffer, controlunit_1_de1, controlunit_1_de2,
       controlunit_1_dm, controlunit_1_dpc, controlunit_1_la, controlunit_1_lb, controlunit_1_ld,
       controlunit_1_lir, controlunit_1_lmar, controlunit_1_lpc, controlunit_1_lrd, controlunit_1_mc,
       controlunit_1_mx1, controlunit_1_pcp, controlunit_1_sel, controlunit_1_st, decoder_1_out0,
       decoder_1_out1, decoder_1_out2, decoder_1_out3, decoder_2_out0, decoder_2_out1, decoder_2_out2,
       decoder_2_out3, LR0_out, LR1_out, LR2_out, LR3_out, ONE_CLOCK_out;
  wire [1:0] IR_q, IR_q_2, IR_q_3, IR_q_4, multiplexer_1_out;
  wire [7:0] A_q, adder_1_out, B_q, controlled_buffer_1_out, D0_out, D1_out, D2_out, D3_out, MAR_q,
       newalu_1_output, PC_q, R0_q, R1_q, R2_q, R3_q, ram_1_data;

  Clock ONE_CLOCK (.out(ONE_CLOCK_out));
  ControlUnit controlunit_1 (
    .ST(controlunit_1_st), .SEL(controlunit_1_sel), .MC(controlunit_1_mc), .LD(controlunit_1_ld),
    .CLR(controlunit_1_clr), .DM(controlunit_1_dm), .LMAR(controlunit_1_lmar), .LA(controlunit_1_la),
    .LB(controlunit_1_lb), .LIR(controlunit_1_lir), .PCP(controlunit_1_pcp), .MX1(controlunit_1_mx1),
    .DE1(controlunit_1_de1), .DE2(controlunit_1_de2), .LRD(controlunit_1_lrd), .LPC(controlunit_1_lpc),
    .DPC(controlunit_1_dpc), .DBUFFER(controlunit_1_dbuffer), .DALU(controlunit_1_dalu), .OPCODE(IR_q_4),
    .CUReset(Clear), .Clock(ONE_CLOCK_out));
  Decoder #(.select(2)) decoder_1 (
    .out0(decoder_1_out0), .out1(decoder_1_out1), .out2(decoder_1_out2), .out3(decoder_1_out3), .sel(IR_q_3),
    .en(controlunit_1_de2));
  Register #(.trigger("falling")) IR (
    .D(controlled_buffer_1_out), .Q({IR_q_4, IR_q_3, IR_q_2, IR_q}), .clk(controlunit_1_lir));  // open: en, clr
  Multiplexer #(.width(2)) multiplexer_1 (
    .in0(IR_q), .in1(IR_q_2), .out(multiplexer_1_out), .sel(controlunit_1_mx1), .en(1'b1));
  and LR0 (LR0_out, decoder_1_out0, controlunit_1_lrd);
  and LR1 (LR1_out, decoder_1_out1, controlunit_1_lrd);
  and LR2 (LR2_out, decoder_1_out2, controlunit_1_lrd);
  and LR3 (LR3_out, decoder_1_out3, controlunit_1_lrd);
  Decoder #(.select(2)) decoder_2 (
    .out0(decoder_2_out0), .out1(decoder_2_out1), .out2(decoder_2_out2), .out3(decoder_2_out3),
    .sel(multiplexer_1_out), .en(controlunit_1_de1));
  Register #(.trigger("falling")) PC (.D(controlled_buffer_1_out), .Q(PC_q), .clk(controlunit_1_lpc));  // open: en, clr
  assign controlled_buffer_1_out = controlunit_1_dpc ? PC_q : 8'bz;  // Controlled_Buffer controlled_buffer_1
  Register #(.trigger("high")) R3 (.D(controlled_buffer_1_out), .Q(R3_q), .clk(LR3_out));  // open: en, clr
  assign D3_out = decoder_2_out3 ? R3_q : 8'bz;  // Controlled_Buffer D3
  assign controlled_buffer_1_out = controlunit_1_dbuffer ? D3_out : 8'bz;  // Controlled_Buffer controlled_buffer_2
  Register #(.trigger("high")) R2 (.D(controlled_buffer_1_out), .Q(R2_q), .clk(LR2_out));  // open: en, clr
  assign D2_out = decoder_2_out2 ? R2_q : 8'bz;  // Controlled_Buffer D2
  assign controlled_buffer_1_out = controlunit_1_dbuffer ? D2_out : 8'bz;  // Controlled_Buffer controlled_buffer_3
  Register #(.trigger("high")) R1 (.D(controlled_buffer_1_out), .Q(R1_q), .clk(LR1_out));  // open: en, clr
  assign D1_out = decoder_2_out1 ? R1_q : 8'bz;  // Controlled_Buffer D1
  assign controlled_buffer_1_out = controlunit_1_dbuffer ? D1_out : 8'bz;  // Controlled_Buffer controlled_buffer_4
  Register #(.trigger("high")) R0 (.D(controlled_buffer_1_out), .Q(R0_q), .clk(LR0_out));  // open: en, clr
  assign D0_out = decoder_2_out0 ? R0_q : 8'bz;  // Controlled_Buffer D0
  assign controlled_buffer_1_out = controlunit_1_dbuffer ? D0_out : 8'bz;  // Controlled_Buffer controlled_buffer_5
  assign controlled_buffer_1_out = controlunit_1_dalu ? newalu_1_output : 8'bz;  // Controlled_Buffer controlled_buffer_6
  assign controlled_buffer_1_out = controlunit_1_pcp ? adder_1_out : 8'bz;  // Controlled_Buffer controlled_buffer_7
  Adder adder_1 (.a(8'h1), .b(PC_q), .out(adder_1_out));  // open: cin, cout
  Register #(.trigger("falling")) B (.D(controlled_buffer_1_out), .Q(B_q), .clk(controlunit_1_lb));  // open: en, clr
  Register #(.trigger("falling")) A (.D(controlled_buffer_1_out), .Q(A_q), .clk(controlunit_1_la));  // open: en, clr
  NewALU newalu_1 (.A(A_q), .B(B_q), .Select(IR_q_4), .Output(newalu_1_output));
  Register #(.trigger("falling")) MAR (
    .D(controlled_buffer_1_out), .Q(MAR_q), .clk(controlunit_1_lmar));  // open: en, clr
  RAM #(.bus("separate")) ram_1 (
    .addr(MAR_q), .din(controlled_buffer_1_out), .data(ram_1_data), .str(controlunit_1_st),
    .sel(controlunit_1_sel), .clk(controlunit_1_mc), .ld(controlunit_1_ld), .clr(controlunit_1_clr));
  assign controlled_buffer_1_out = controlunit_1_dm ? ram_1_data : 8'bz;  // Controlled_Buffer controlled_buffer_8

  // Notes on the sheet:
  //   ALUOUtput
endmodule

// ALU
module NewALU (
  input  [7:0] A,
  input  [7:0] B,
  input  [1:0] Select,
  output [7:0] Output
);

  wire [7:0] adder_1_out, and_1_out, or_1_out;

  assign and_1_out = B & A;  // AND_Gate and_1, 8 bits wide
  assign or_1_out = B | A;  // OR_Gate or_1, 8 bits wide
  Adder adder_1 (.a(A), .b(B), .out(adder_1_out));  // open: cin, cout
  Multiplexer #(.select(2), .width(8)) multiplexer_1 (
    .in0(adder_1_out), .in1(and_1_out), .in2(or_1_out), .in3(A), .out(Output), .sel(Select));  // open: en
endmodule

module ControlUnit (
  input  [1:0] OPCODE,
  input  CUReset,
  input  Clock,
  output ST,
  output SEL,
  output MC,
  output LD,
  output CLR,
  output DM,
  output LMAR,
  output LA,
  output LB,
  output LIR,
  output PCP,
  output MX1,
  output DE1,
  output DE2,
  output LRD,
  output LPC,
  output DPC,
  output DBUFFER,
  output DALU
);

  wire [3:0] multiplexer_1_out, register_1_q, rom_2_data;
  wire [4:0] rom_1_data;

  Register #(.width(4)) register_1 (.D(multiplexer_1_out), .Q(register_1_q), .clk(Clock), .clr(CUReset));  // open: en
  ROM #(.addrWidth(4), .dataWidth(24)) rom_1 (
    .addr(register_1_q),
    .data({ST, SEL, MC, LD, CLR, DM, LMAR, LA, LB, LIR, PCP, MX1, DE1, DE2, LRD, LPC, DPC, DBUFFER, DALU, rom_1_data}),
    .sel(1'b1));
  Multiplexer #(.width(4), .enable("false")) multiplexer_1 (
    .in0(rom_1_data[3:0]), .in1(rom_2_data), .out(multiplexer_1_out), .sel(rom_1_data[4]));
  ROM #(.addrWidth(2), .dataWidth(4)) rom_2 (.addr(OPCODE), .data(rom_2_data), .sel(1'b1));

  // Notes on the sheet:
  //   MAIN ROM 
  //   IMAGE: MAIN CU ROM
  //   contents of rom_1 (hex, n*v repeats v):
  //   1 20082 744003 2114 11845 8846 621 11848 8849 621 1184b 884c 621 2184e 740601
  //   contents of rom_2 (hex, n*v repeats v):
  //   4 7 a d
  //   IMAGE: addressTOROM
  //   OPCODE TO ADDRESS 
endmodule
